# Fritzing sketch BaseStation (saved by Fritzing 0.9.3b)
breadboards: 1

parts:
  Transceiver = NRF24L01+ Breakout Board
  GSM_Module = SIM800L [package=THT]
  MCU = BluePill
  PSU = YwRobot Breadboard Power Supply [part_number=545043]

nets:
  GND: Transceiver.GND, GSM_Module.GND#5, MCU.GND, PSU.GND#13
  VCC: Transceiver.VCC, GSM_Module.VDD, MCU.3V3, PSU.VCC#9
  N1: Transceiver.CE, MCU.B0
  N2: Transceiver.CS, MCU.A4
  N3: Transceiver.SCK, MCU.A5
  N4: Transceiver.MOSI, MCU.A7
  N5: Transceiver.MISO, MCU.A6
  N6: Transceiver.IRQ, MCU.B1
  N7: GSM_Module.SIM_TXD, MCU.A3
  N8: GSM_Module.SIM_RXD, MCU.A2
  N9: GSM_Module.RST, MCU.NRST

custom parts:
  BluePill: Generic ebay blue pill STM32F103C8 "Blue pill" CPU module. Arm Cortex M3 128KB flash (usually) 20kb ram, RTC on board. Supported by the Arduino IDE for programming. As cheap as an Arduino nano but with more power and memory.
  YwRobot Breadboard Power Supply: The YwRobot Breadboard Power Supply (MB-V2) has two power rails; they can be 5V or 3V3. Power to the module can be provided through the female USB socket or through the A10 (female) 2.1mm power jack.
