# Fritzing sketch RemoteUnit (saved by Fritzing 0.9.3b)
breadboards: 1

parts:
  MCU = BluePill
  Receiver = NRF24L01+ Breakout Board
  R1 = Resistor [tolerance=±5% resistance=1k package="0603 [SMD]"]
  R2 = Resistor [tolerance=±5% resistance=1k package="0603 [SMD]"]
  LED2 = LED - 3mm [color="Yellow (595nm)" package="3 mm [THT]"]
  LED3 = LED - 3mm [color="Red (660nm)" package="3 mm [THT]"]

nets (from the breadboard view):
  N1: MCU.C14, R2.Pin_0
  N2: MCU.C15, R1.Pin_0
  N3: MCU.A2, Receiver.IRQ
  N4: MCU.A3, Receiver.CE
  N5: MCU.A4, Receiver.CS
  N6: MCU.A5, Receiver.SCK
  N7: MCU.A6, Receiver.MISO
  N8: MCU.A7, Receiver.MOSI
  3V3: MCU.3V3, Receiver.VCC, LED2.anode, LED3.anode
  GND: MCU.GND, Receiver.GND
  N9: R1.Pin_1, LED3.cathode
  N10: R2.Pin_1, LED2.cathode

custom parts:
  BluePill: Generic ebay blue pill STM32F103C8 "Blue pill" CPU module. Arm Cortex M3 128KB flash (usually) 20kb ram, RTC on board. Supported by the Arduino IDE for programming. As cheap as an Arduino nano but with more power and memory.
